# Fritzing sketch esquema (saved by Fritzing 0.9.2b)
stripboards: 1

parts:
  Parte1 = Arduino Nano (Rev3.0)
  Q1 = TIP120 Hi-Current Darlington Transistor
  Q2 = TIP120 Hi-Current Darlington Transistor
  Q3 = TIP120 Hi-Current Darlington Transistor
  LPD8806_RGB_LED_Strip1 = LPD8806 RGB LED Strip
  J1 = COMPUTER-PERIPHERAL-POWER [package=computer-peripheral-power]
  S1 = Round Pushbutton
  R1 = Resistor [tolerance=±5% resistance=10k package=THT]

nets:
  N1: Parte1.D2, S1.leg0, R1.Pin_0
  N2: Parte1.D3, Q3.BASE
  N3: Parte1.D6, Q2.BASE
  N4: Parte1.D9, Q1.BASE
  VIN: Parte1.VIN, J1.12V
  GND: Parte1.GND, Q1.COLLECTOR, Q2.COLLECTOR, Q3.COLLECTOR, J1.GND, J1.NC
  N5: Q1.EMITTER, LPD8806_RGB_LED_Strip1.R
  N6: Q2.EMITTER, LPD8806_RGB_LED_Strip1.G
  N7: Q3.EMITTER, LPD8806_RGB_LED_Strip1.+12V
  N8: LPD8806_RGB_LED_Strip1.B, J1.5V

custom parts:
  LPD8806 RGB LED Strip: Digitally addressable RGB LED strip
