# Fritzing sketch esquema_compacto (saved by Fritzing 0.9.2b)
perfboards: 1

parts:
  LPD8806_RGB_LED_Strip1 = LPD8806 RGB LED Strip
  Parte2 = Arduino Nano (Rev3.0)
  Q4 = TIP120 Hi-Current Darlington Transistor
  Q5 = TIP120 Hi-Current Darlington Transistor
  Q6 = TIP120 Hi-Current Darlington Transistor
  S2 = Round Pushbutton
  J4 = COMPUTER-PERIPHERAL-POWER [package=computer-peripheral-power]
  JP1 = Header 1 [package=1x01_offset]
  JP2 = Header 1 [package=1x01_offset]
  LED2 = LED - 3mm [color="Red (635nm)" package="3 mm [THT]"]

nets:
  N1: LPD8806_RGB_LED_Strip1.+12V, Q4.COLLECTOR
  N2: LPD8806_RGB_LED_Strip1.G, Q6.COLLECTOR
  N3: LPD8806_RGB_LED_Strip1.R, Q5.COLLECTOR
  N4: LPD8806_RGB_LED_Strip1.B, J4.5V
  GND: Parte2.GND, Q4.EMITTER, Q6.EMITTER, J4.GND, J4.NC, JP1.1
  N5: Parte2.D2, S2.leg0
  N6: Parte2.D3, Q6.BASE
  N7: Parte2.D4, Q5.BASE
  VIN: Parte2.VIN, J4.12V, JP2.1
  N8: Parte2.D13/SCK, LED2.cathode
  N9: S2.leg1, LED2.anode

custom parts:
  LPD8806 RGB LED Strip: Digitally addressable RGB LED strip

// code stored in the sketch: Tira-de-led-Arduino.ino
/**
   @file Tira-de-led-Arduino.ino
   @brief Gestion de una tira de led
   @author Pablo Rocamora pablojoserocamora@gmail.com
   @date 14/12/2016
*/

//Info: http://www.prometec.net/tira-de-leds/

#define DEBUG true

#define LED_R 3      //ROJO
#define LED_G 4      //VERDE
#define LED_B 5      //AZUL
#define BUTTON 6     //Conexion del boton

//inicio contador en 1 para que en la primera pulsacion entre en el rojo
int contador = 1;
boolean lastButton = LOW;   //contiene el estado anterioR del boton
boolean currentButton = LOW;  //Contiene el estado actual del boton

void setup() {
  pinMode (LED_R, OUTPUT);
  pinMode (LED_G, OUTPUT);
  pinMode (LED_B, OUTPUT);
  pinMode(BUTTON, INPUT_PULLUP);   // Para leel el boton
  pinMode(13, OUTPUT);         // Para usar un LED de encendido
  if (DEBUG) {
    Serial.begin(115200);
    Serial.println("inicio");
  }
}


/*
  Debouncing Function
  Pass it the previous button state,
  and get back the current debounced button state.
*/
boolean debounce(boolean last) {
  boolean current = digitalRead(BUTTON);    //Read the button state
  if (last != current) {            //if it's different?
    delay(5);               //wait 5ms
    current = digitalRead(BUTTON);      //read it again
  }
  return current;               //return the current value
}


void loop() {
  currentButton = debounce(lastButton);       //read debounced state
  if (lastButton == LOW && currentButton == HIGH) {  //if it was pressed?
    if (DEBUG)
      Serial.println("CONTADOR: " + String(contador));
    //delay(500);

    switch (contador) {
      case 0:
        if (DEBUG)
          Serial.println("APAGAR");
        contador++;
        digitalWrite(LED_R, LOW);
        digitalWrite(LED_G, LOW);
        digitalWrite(LED_B, LOW);
        break;

      case 1: //ROJO
        if (DEBUG)
          Serial.println("rojo");
        contador++;
        digitalWrite(LED_R, HIGH);
        digitalWrite(LED_G, LOW);
        digitalWrite(LED_B, LOW);
        break;

      case 2: //VERDE
        if (DEBUG)
          Serial.println("verde");
        contador++;
        digitalWrite(LED_R, LOW);
        digitalWrite(LED_G, HIGH);
        digitalWrite(LED_B, LOW);
        break;

      case 3: //AZUL
        if (DEBUG)
          Serial.println("azul");
        contador = 0;
        digitalWrite(LED_R, LOW);
        digitalWrite(LED_G, LOW);
        digitalWrite(LED_B, HIGH);
        break;

      default:  //nunca debria llegar aqui
        contador = 0;
        if (DEBUG) {
          Serial.println("HAY ALGUN FALLO CON EL CONTADOR");
          Serial.println(contador);
        }
        break;
    }
  }

  lastButton = currentButton;
}
